// Logisim project alu.circ as structural Verilog: 2 circuits, main circuit alu
module alu (
  input  [31:0] A,
  input  [31:0] B,
  input  [3:0] ALUSel,
  output [31:0] Result
);

  wire comparator_1_lt;
  wire [31:0] add0, and0, divu0, mul0, mulh0, mulhu0, or0, remu0, sll0, slt0, sra0, srl0, sub0, xor0;

  Multiplexer #(.select(4), .width(32), .enable("false")) multiplexer_1 (
    .in0(add0), .in1(and0), .in2(or0), .in3(xor0), .in4(srl0), .in5(sra0), .in6(sll0), .in7(slt0),
    .in8(divu0), .in9(remu0), .in10(mul0), .in11(mulhu0), .in12(sub0), .in13(B), .in14(mulh0),
    .in15({32{1'b0}}), .out(Result), .sel(ALUSel));
  Adder #(.width(32)) adder_1 (.a(A), .b(B), .out(add0));  // open: cin, cout
  assign and0 = A & B;  // AND_Gate and_1, 32 bits wide
  assign or0 = A | B;  // OR_Gate or_1, 32 bits wide
  assign xor0 = A ^ B;  // XOR_Gate xor_1, 32 bits wide
  Shifter #(.width(32), .shift("lr")) shifter_1 (.in(A), .\dist (B[4:0]), .out(srl0));
  Shifter #(.width(32), .shift("ar")) shifter_2 (.in(A), .\dist (B[4:0]), .out(sra0));
  Shifter #(.width(32)) shifter_3 (.in(A), .\dist (B[4:0]), .out(sll0));
  Comparator #(.width(32)) comparator_1 (.a(A), .b(B), .lt(comparator_1_lt));  // open: gt, eq
  Divider #(.width(32)) divider_1 (.a(A), .b(B), .out(divu0), .rem(remu0));  // open: upper
  Subtractor #(.width(32)) subtractor_1 (.a(A), .b(B), .out(sub0));  // open: bin, bout
  assign slt0 = {{31{1'b0}}, comparator_1_lt};  // Bit_Extender bit_extender_1
  my_mul my_mul_1 (.InputA(A), .InputB(B), .Output_mul(mul0), .Output_mulhu(mulhu0), .Output_mulh(mulh0));

  // Notes on the sheet:
  //   INPUTS to your circuit
  //   DON'T CHANGE THE LOCATIONS OF THE INPUTS AND OUTPUTS!
  //   OUTPUT from your circuit
endmodule

module my_mul (
  input  [31:0] InputA,
  input  [31:0] InputB,
  output [31:0] Output_mul,
  output [31:0] Output_mulhu,
  output [31:0] Output_mulh
);

  wire [31:0] negator_1_out, negator_2_out, output01, output10, output11;

  Multiplexer #(.select(2), .width(32), .enable("false")) multiplexer_1 (
    .in0(Output_mulhu), .in1(output01), .in2(output10), .in3(output11), .out(Output_mulh),
    .sel({InputB[31], InputA[31]}));
  Negator #(.width(32)) negator_1 (.in(InputA), .out(negator_1_out));
  Negator #(.width(32)) negator_2 (.in(InputB), .out(negator_2_out));
  Multiplier #(.width(32)) multiplier_1 (.a(negator_1_out), .b(negator_2_out), .cout(output11));  // open: out, cin
  Multiplier #(.width(32)) multiplier_2 (.a(InputA), .b(InputB), .out(Output_mul), .cout(Output_mulhu));  // open: cin
  Multiplier #(.width(32)) multiplier_3 (.a(InputA), .b({32{1'b1}}), .out(output10), .cin(Output_mulhu));  // open: cout
  Multiplier #(.width(32)) multiplier_4 (.a(InputB), .b({32{1'b1}}), .out(output01), .cin(Output_mulhu));  // open: cout

  // Other names for the same wires on the sheet: A[31:0] = InputA; input0[31:0] = InputA; sign0 = InputA[31];
  //   B[31:0] = InputB; input1[31:0] = InputB; sign1 = InputB[31]; output00[31:0] = Output_mulhu
endmodule
