// Logisim project branch_comp.circ as structural Verilog: 1 circuit, main circuit branch_comp
module branch_comp (
  input  [31:0] rs1,
  input  [31:0] rs2,
  input  BrUn,
  output BrEq,
  output BrLt
);

  wire BrEq_2s, BrEq_unsign, BrLt_2s, BrLt_unsign;

  Multiplexer #(.enable("false")) multiplexer_1 (.in0(BrEq_2s), .in1(BrEq_unsign), .out(BrEq), .sel(BrUn));
  Comparator #(.width(32), .mode("unsigned")) comparator_1 (
    .a(rs1), .b(rs2), .eq(BrEq_unsign), .lt(BrLt_unsign));  // open: gt
  Comparator #(.width(32)) comparator_2 (.a(rs1), .b(rs2), .eq(BrEq_2s), .lt(BrLt_2s));  // open: gt
  Multiplexer #(.enable("false")) multiplexer_2 (.in0(BrLt_2s), .in1(BrLt_unsign), .out(BrLt), .sel(BrUn));

  // Notes on the sheet:
  //   INPUTS to your circuit
  //   DON'T CHANGE THE LOCATIONS OF THE INPUTS AND OUTPUTS!
  //   OUTPUT from your circuit
endmodule
