// Logisim project control_logic.circ as structural Verilog: 8 circuits, main circuit control_logic
module control_logic (
  input  [31:0] inst,
  input  BrEq,
  input  BrLt,
  output out_4,
  output RegWEn,
  output [2:0] ImmSel,
  output BrUn,
  output ASel,
  output BSel,
  output [3:0] ALUSel,
  output MemRW,
  output [1:0] WBSel
);

  wire comparator_1_eq;

  pcsel_logic pcsel_logic_1 (.opcode(inst[6:0]), .funct3(inst[14:12]), .breq(BrEq), .brlt(BrLt), .pcsel(out_4));
  regwen_logic regwen_logic_1 (.opcode(inst[6:0]), .regwen(RegWEn));
  immsel_logic immsel_logic_1 (.opcode(inst[6:0]), .immsel(ImmSel));
  Comparator #(.width(7)) comparator_1 (.a(inst[6:0]), .b(7'b0110011), .eq(comparator_1_eq));  // open: gt, lt
  Comparator #(.width(3), .mode("unsigned")) comparator_2 (.a(inst[14:12]), .b(3'b101), .gt(BrUn));  // open: eq, lt
  not not_1 (BSel, comparator_1_eq);
  asel_logic asel_logic_1 (.opcode(inst[6:0]), .asel(ASel));
  alusel_logic alusel_logic_1 (.opcode(inst[6:0]), .funct3(inst[14:12]), .funct7(inst[31:25]), .alusel(ALUSel));
  memrw_logic memrw_logic_1 (.opcode(inst[6:0]), .funct3(inst[14:12]), .breq(BrEq), .brlt(BrLt), .memrw(MemRW));
  wbsel_logic wbsel_logic_1 (.opcode(inst[6:0]), .wbsel(WBSel));

  // Other names for the same wires on the sheet: Opcode[6:0] = inst[6:0]; Funct3[2:0] = inst[14:12];
  //   Funct7[6:0] = inst[31:25]; PcSel = out_4

  // Notes on the sheet:
  //   INPUTS to your circuit
  //   DON'T CHANGE THE LOCATIONS OF THE INPUTS AND OUTPUTS!
  //   OUTPUT from your circuit
endmodule

module pcsel_logic (
  input  [6:0] opcode,
  input  [2:0] funct3,
  input  breq,
  input  brlt,
  output pcsel
);

  wire and_1_out, comparator_1_eq, comparator_2_eq, comparator_3_eq, multiplexer_1_out, not_1_out, not_2_out;

  not not_1 (not_1_out, breq);
  not not_2 (not_2_out, brlt);
  Comparator #(.width(7), .mode("unsigned")) comparator_1 (
    .a(opcode), .b(7'b1100011), .eq(comparator_1_eq));  // open: gt, lt
  Multiplexer #(.select(3), .enable("false")) multiplexer_1 (
    .in0(breq), .in1(not_1_out), .in4(brlt), .in5(not_2_out), .in6(brlt), .in7(not_2_out),
    .out(multiplexer_1_out), .sel(funct3));  // open: in2, in3
  Comparator #(.width(7), .mode("unsigned")) comparator_2 (
    .a(opcode), .b(7'b1100111), .eq(comparator_2_eq));  // open: gt, lt
  Comparator #(.width(7), .mode("unsigned")) comparator_3 (
    .a(opcode), .b(7'b1101111), .eq(comparator_3_eq));  // open: gt, lt
  and and_1 (and_1_out, multiplexer_1_out, comparator_1_eq);
  or or_1 (pcsel, and_1_out, comparator_2_eq, comparator_3_eq);

  // Other names for the same wires on the sheet: pcsel_intput[6:0] = opcode; pcsel_output = pcsel
endmodule

module regwen_logic (
  input  [6:0] opcode,
  output regwen
);

  wire comparator_1_eq, comparator_2_eq, not_1_out, not_2_out;

  Comparator #(.width(7)) comparator_1 (.a(opcode), .b(7'b1100011), .eq(comparator_1_eq));  // open: gt, lt
  Comparator #(.width(7)) comparator_2 (.a(opcode), .b(7'b0100011), .eq(comparator_2_eq));  // open: gt, lt
  not not_1 (not_1_out, comparator_1_eq);
  not not_2 (not_2_out, comparator_2_eq);
  and and_1 (regwen, not_1_out, not_2_out);
endmodule

module immsel_logic (
  input  [6:0] opcode,
  output [2:0] immsel
);

  wire A, and_1_out, and_4_out, B, C, comparator_1_eq, comparator_2_eq, comparator_3_eq, comparator_6_eq,
       comparator_7_eq, D, E, not_1_out, not_2_out, not_3_out, not_4_out, not_5_out, not_6_out, not_7_out,
       not_8_out, not_9_out, not_10_out, not_11_out, or_3_out, xor_1_out, xor_2_out, xor_3_out;

  Comparator #(.width(7)) comparator_1 (.a(opcode), .b(7'b1100111), .eq(comparator_1_eq));  // open: gt, lt
  Comparator #(.width(7)) comparator_2 (.a(opcode), .b(7'b0010011), .eq(comparator_2_eq));  // open: gt, lt
  Comparator #(.width(7)) comparator_3 (.a(opcode), .b(7'b0000011), .eq(comparator_3_eq));  // open: gt, lt
  Comparator #(.width(7)) comparator_4 (.a(opcode), .b(7'b0100011), .eq(D));  // open: gt, lt
  Comparator #(.width(7)) comparator_5 (.a(opcode), .b(7'b1100011), .eq(C));  // open: gt, lt
  Comparator #(.width(7)) comparator_6 (.a(opcode), .b(7'b0010111), .eq(comparator_6_eq));  // open: gt, lt
  Comparator #(.width(7)) comparator_7 (.a(opcode), .b(7'b0110111), .eq(comparator_7_eq));  // open: gt, lt
  Comparator #(.width(7)) comparator_8 (.a(opcode), .b(7'b1101111), .eq(A));  // open: gt, lt
  or or_1 (E, comparator_1_eq, comparator_2_eq, comparator_3_eq);
  or or_2 (B, comparator_6_eq, comparator_7_eq);
  xor xor_1 (xor_1_out, B, A);
  not not_1 (not_1_out, C);
  not not_2 (not_2_out, D);
  not not_3 (not_3_out, E);
  xor xor_2 (xor_2_out, C, D);
  not not_4 (not_4_out, A);
  not not_5 (not_5_out, B);
  not not_6 (not_6_out, E);
  not not_7 (not_7_out, A);
  not not_8 (not_8_out, C);
  not not_9 (not_9_out, E);
  xor xor_3 (xor_3_out, A, C);
  and and_1 (and_1_out, E, not_8_out, not_7_out);
  and and_2 (immsel[2], xor_1_out, not_1_out, not_2_out, not_3_out);
  and and_3 (immsel[1], xor_2_out, not_4_out, not_5_out, not_6_out);
  and and_4 (and_4_out, xor_3_out, not_9_out);
  or or_3 (or_3_out, and_4_out, and_1_out);
  not not_10 (not_10_out, B);
  not not_11 (not_11_out, D);
  and and_5 (immsel[0], or_3_out, not_10_out, not_11_out);

  // Other names for the same wires on the sheet: one = immsel[0]; two = immsel[1]; three = immsel[2]
endmodule

module asel_logic (
  input  [6:0] opcode,
  output asel
);

  wire comparator_1_eq, comparator_2_eq, comparator_3_eq;

  Comparator #(.width(7)) comparator_1 (.a(opcode), .b(7'b1100011), .eq(comparator_1_eq));  // open: gt, lt
  Comparator #(.width(7)) comparator_2 (.a(opcode), .b(7'b0010111), .eq(comparator_2_eq));  // open: gt, lt
  Comparator #(.width(7)) comparator_3 (.a(opcode), .b(7'b1101111), .eq(comparator_3_eq));  // open: gt, lt
  or or_1 (asel, comparator_1_eq, comparator_2_eq, comparator_3_eq);
endmodule

module alusel_logic (
  input  [6:0] opcode,
  input  [2:0] funct3,
  input  [6:0] funct7,
  output [3:0] alusel
);

  wire and_3_out, and_4_out, and_13_out, and_14_out, and_15_out, and_16_out, and_17_out, and_23_out,
       and_24_out, and_25_out, and_26_out, and_27_out, and_28_out, and_34_out, and_35_out, and_36_out,
       and_37_out, and_38_out, and_39_out, I0000, II0000, IR0000, Is_IR, Is_R, not_1_out, not_2_out,
       not_3_out, not_4_out, not_5_out, not_6_out, not_7_out, not_8_out, not_9_out, not_10_out, not_11_out,
       not_12_out, not_13_out, not_14_out, not_15_out, not_16_out, not_17_out, not_18_out, not_19_out,
       not_20_out, not_21_out, not_22_out, not_23_out, not_24_out, not_25_out, not_26_out, not_27_out,
       not_28_out, not_29_out, not_30_out, not_31_out, not_32_out, not_33_out, not_34_out, not_35_out,
       not_36_out, not_37_out, not_38_out, not_39_out, not_40_out, not_41_out, not_42_out, not_43_out,
       not_44_out, not_45_out, not_46_out, not_47_out, not_48_out, not_49_out, not_50_out, not_51_out,
       not_52_out, not_53_out, not_54_out, not_55_out, or_2_out, or_3_out, or_4_out, or_5_out, or_6_out,
       or_7_out, OUT0000, OUT0001, OUT0010, OUT0011, OUT0100, OUT0101, OUT0110, OUT0111, OUT1000, OUT1001,
       OUT1010, OUT1011, OUT1100, OUT1110, R0000, S0000, SB0000, U0000, UJ0000;
  wire [3:0] bitfinder_1_index;

  not not_1 (not_1_out, opcode[2]);
  not not_2 (not_2_out, opcode[3]);
  not not_3 (not_3_out, opcode[4]);
  not not_4 (not_4_out, opcode[4]);
  not not_5 (not_5_out, opcode[3]);
  not not_6 (not_6_out, opcode[6]);
  not not_7 (not_7_out, opcode[3]);
  not not_8 (not_8_out, opcode[4]);
  not not_9 (not_9_out, funct3[0]);
  not not_10 (not_10_out, funct3[1]);
  not not_11 (not_11_out, funct3[2]);
  not not_12 (not_12_out, funct7[0]);
  not not_13 (not_13_out, funct7[5]);
  not not_14 (not_14_out, funct3[0]);
  not not_15 (not_15_out, funct3[1]);
  not not_16 (not_16_out, funct3[2]);
  and and_1 (SB0000, not_1_out, not_2_out, not_3_out, opcode[5], opcode[6]);
  and and_2 (UJ0000, opcode[2], opcode[3], not_4_out, opcode[5], opcode[6]);
  and and_3 (and_3_out, not_9_out, not_10_out, not_11_out);
  and and_4 (and_4_out, not_14_out, not_15_out, not_16_out);
  and and_5 (U0000, opcode[2], not_5_out, opcode[4], not_6_out);
  and and_6 (I0000, opcode[2], not_7_out, not_8_out, opcode[5], opcode[6]);
  and and_7 (IR0000, Is_IR, and_3_out);
  and and_8 (R0000, Is_R, not_12_out, not_13_out, and_4_out);
  not not_17 (not_17_out, opcode[2]);
  not not_18 (not_18_out, opcode[3]);
  not not_19 (not_19_out, opcode[4]);
  not not_20 (not_20_out, opcode[6]);
  not not_21 (not_21_out, opcode[2]);
  not not_22 (not_22_out, opcode[3]);
  not not_23 (not_23_out, opcode[4]);
  not not_24 (not_24_out, opcode[5]);
  not not_25 (not_25_out, opcode[6]);
  not not_26 (not_26_out, opcode[2]);
  not not_27 (not_27_out, opcode[3]);
  not not_28 (not_28_out, opcode[5]);
  not not_29 (not_29_out, opcode[6]);
  not not_30 (not_30_out, opcode[2]);
  not not_31 (not_31_out, opcode[3]);
  not not_32 (not_32_out, opcode[6]);
  or or_1 (OUT0000, SB0000, UJ0000, U0000, I0000, IR0000, R0000, S0000, II0000);
  and and_9 (S0000, not_17_out, not_18_out, not_19_out, opcode[5], not_20_out);
  and and_10 (II0000, not_21_out, not_22_out, not_23_out, not_24_out, not_25_out);
  and and_11 (Is_IR, not_26_out, not_27_out, opcode[4], not_28_out, not_29_out);
  and and_12 (Is_R, not_30_out, not_31_out, opcode[4], opcode[5], not_32_out);
  not not_33 (not_33_out, funct3[0]);
  not not_34 (not_34_out, funct3[1]);
  not not_35 (not_35_out, funct7[0]);
  not not_36 (not_36_out, funct3[1]);
  not not_37 (not_37_out, funct3[2]);
  not not_38 (not_38_out, funct3[0]);
  not not_39 (not_39_out, funct3[2]);
  not not_40 (not_40_out, funct3[0]);
  not not_41 (not_41_out, funct3[1]);
  not not_42 (not_42_out, funct3[2]);
  not not_43 (not_43_out, funct3[0]);
  not not_44 (not_44_out, funct3[1]);
  not not_45 (not_45_out, funct3[2]);
  or or_2 (or_2_out, Is_IR, Is_R);
  and and_13 (and_13_out, not_33_out, not_34_out, funct3[2]);
  or or_3 (or_3_out, Is_IR, Is_R);
  and and_14 (and_14_out, funct3[0], not_36_out, not_37_out);
  or or_4 (or_4_out, Is_IR, Is_R);
  and and_15 (and_15_out, not_38_out, funct3[1], not_39_out);
  and and_16 (and_16_out, not_40_out, not_41_out, not_42_out);
  and and_17 (and_17_out, not_43_out, not_44_out, not_45_out);
  and and_18 (OUT0011, or_2_out, and_13_out);
  and and_19 (OUT0110, or_3_out, not_35_out, and_14_out);
  and and_20 (OUT0111, or_4_out, and_15_out);
  and and_21 (OUT1100, Is_R, funct7[5], and_16_out);
  and and_22 (OUT1010, Is_R, funct7[0], and_17_out);
  not not_46 (not_46_out, funct3[0]);
  not not_47 (not_47_out, funct7[5]);
  not not_48 (not_48_out, funct7[0]);
  not not_49 (not_49_out, funct3[1]);
  not not_50 (not_50_out, funct3[1]);
  not not_51 (not_51_out, funct3[1]);
  not not_52 (not_52_out, funct3[2]);
  not not_53 (not_53_out, funct3[1]);
  or or_5 (or_5_out, Is_IR, Is_R);
  and and_23 (and_23_out, not_46_out, funct3[1], funct3[2]);
  or or_6 (or_6_out, Is_IR, Is_R);
  and and_24 (and_24_out, not_47_out, not_48_out);
  and and_25 (and_25_out, funct3[0], not_49_out, funct3[2]);
  or or_7 (or_7_out, Is_IR, Is_R);
  and and_26 (and_26_out, funct3[0], not_50_out, funct3[2]);
  and and_27 (and_27_out, funct3[0], not_51_out, not_52_out);
  and and_28 (and_28_out, funct3[0], not_53_out, funct3[2]);
  and and_29 (OUT0010, or_5_out, and_23_out);
  and and_30 (OUT0100, or_6_out, and_24_out, and_25_out);
  and and_31 (OUT0101, or_7_out, funct7[5], and_26_out);
  and and_32 (OUT1110, Is_R, funct7[0], and_27_out);
  and and_33 (OUT1000, Is_R, funct7[0], and_28_out);
  and and_34 (and_34_out, funct3[0], funct3[1], funct3[2]);
  not not_54 (not_54_out, funct7[0]);
  not not_55 (not_55_out, funct3[2]);
  and and_35 (and_35_out, funct3[0], funct3[1], funct3[2]);
  and and_36 (and_36_out, funct3[0], funct3[1], not_55_out);
  and and_37 (and_37_out, funct3[0], funct3[1], funct3[2]);
  and and_38 (and_38_out, Is_IR, and_34_out);
  and and_39 (and_39_out, Is_R, not_54_out, and_35_out);
  and and_40 (OUT1011, Is_R, funct7[0], and_36_out);
  and and_41 (OUT1001, Is_R, funct7[0], and_37_out);
  or or_8 (OUT0001, and_38_out, and_39_out);
  BitFinder #(.width(14)) bitfinder_1 (
    .in({OUT1110, OUT1100, OUT1011, OUT1010, OUT1001, OUT1000, OUT0111, OUT0110, OUT0101, OUT0100, OUT0011, OUT0010, OUT0001, OUT0000}),
    .index(bitfinder_1_index));  // open: found
  Multiplexer #(.select(4), .width(4), .enable("false")) multiplexer_1 (
    .in0(4'b0000), .in1(4'b0001), .in2(4'b0010), .in3(4'b0011), .in4(4'b0100), .in5(4'b0101), .in6(4'b0110),
    .in7(4'b0111), .in8(4'b1000), .in9(4'b1001), .in10(4'b1010), .in11(4'b1011), .in12(4'b1100),
    .in13(4'b1110), .out(alusel), .sel(bitfinder_1_index));  // open: in14, in15

  // Notes on the sheet:
  //   INPUT
  //   OUTPUT
endmodule

module memrw_logic (
  input  [6:0] opcode,
  input  [2:0] funct3,
  input  breq,
  input  brlt,
  output memrw
);

  wire and_1_out, and_2_out, comparator_1_eq, comparator_2_eq, comparator_3_eq, not_1_out;

  Comparator #(.width(7), .mode("unsigned")) comparator_1 (
    .a(opcode), .b(7'b0100011), .eq(comparator_1_eq));  // open: gt, lt
  Comparator #(.width(3), .mode("unsigned")) comparator_2 (
    .a(funct3), .b(3'b010), .eq(comparator_2_eq));  // open: gt, lt
  Comparator #(.width(3), .mode("unsigned")) comparator_3 (
    .a(funct3), .b(3'b111), .eq(comparator_3_eq));  // open: gt, lt
  not not_1 (not_1_out, breq);
  and and_1 (and_1_out, comparator_1_eq, comparator_2_eq);
  and and_2 (and_2_out, comparator_1_eq, comparator_3_eq, brlt, not_1_out);
  or or_1 (memrw, and_1_out, and_2_out);
endmodule

module wbsel_logic (
  input  [6:0] opcode,
  output [1:0] wbsel
);

  wire comparator_1_eq, comparator_2_eq, comparator_3_eq, comparator_4_eq, comparator_5_eq, one, three, two,
       zero;
  wire [1:0] bitfinder_1_index;

  Comparator #(.width(7)) comparator_1 (.a(opcode), .b(7'b1101111), .eq(comparator_1_eq));  // open: gt, lt
  Comparator #(.width(7)) comparator_2 (.a(opcode), .b(7'b1100111), .eq(comparator_2_eq));  // open: gt, lt
  Comparator #(.width(7)) comparator_3 (.a(opcode), .b(7'b0010011), .eq(comparator_3_eq));  // open: gt, lt
  Comparator #(.width(7)) comparator_4 (.a(opcode), .b(7'b0110011), .eq(comparator_4_eq));  // open: gt, lt
  Comparator #(.width(7)) comparator_5 (.a(opcode), .b(7'b0010111), .eq(comparator_5_eq));  // open: gt, lt
  Comparator #(.width(7)) comparator_6 (.a(opcode), .b(7'b0000011), .eq(two));  // open: gt, lt
  Comparator #(.width(7)) comparator_7 (.a(opcode), .b(7'b0110111), .eq(three));  // open: gt, lt
  or or_1 (zero, comparator_1_eq, comparator_2_eq);
  or or_2 (one, comparator_3_eq, comparator_4_eq, comparator_5_eq);
  BitFinder #(.width(4)) bitfinder_1 (.in({three, two, one, zero}), .index(bitfinder_1_index));  // open: found
  Multiplexer #(.select(2), .width(2), .enable("false")) multiplexer_1 (
    .in0(2'b00), .in1(2'b01), .in2(2'b10), .in3(2'b11), .out(wbsel), .sel(bitfinder_1_index));
endmodule
