// Logisim project cpu.circ as structural Verilog: 2 circuits, main circuit main
module main (
  input  [31:0] INSTRUCTION,
  input  CLOCK,
  output [31:0] PROGRAM_COUNTER,
  output [31:0] ra,
  output [31:0] sp,
  output [31:0] t0,
  output [31:0] t1,
  output [31:0] t2,
  output [31:0] s0,
  output [31:0] s1,
  output [31:0] a0
);

  wire asel, breq, brlt, brun, bsel, memrw, pcsel, regwen;
  wire [1:0] wbsel;
  wire [2:0] immsel;
  wire [3:0] alusel;
  wire [31:0] adder_1_out, alu_result, dmem, imm, instruction_curr, multiplexer_1_out, multiplexer_2_out,
       multiplexer_3_out, multiplexer_4_out, output_dmem, pc_value, pc_value_plus_4, rs1, rs2, wb;

  Adder #(.width(32)) adder_1 (.a(PROGRAM_COUNTER), .b(32'h4), .out(adder_1_out));  // open: cin, cout
  control_logic control_logic_1 (
    .BSel(bsel), .ASel(asel), .BrUn(brun), .ImmSel(immsel), .RegWEn(regwen), .out_4(pcsel), .BrLt(brlt),
    .BrEq(breq), .inst(instruction_curr), .ALUSel(alusel), .MemRW(memrw), .WBSel(wbsel));
  Multiplexer #(.width(32), .enable("false")) multiplexer_1 (
    .in0(adder_1_out), .in1(alu_result), .out(multiplexer_1_out), .sel(pcsel));
  Register #(.width(32)) PC (.D(multiplexer_1_out), .clk(CLOCK), .Q(PROGRAM_COUNTER));  // open: en, clr
  Multiplexer #(.width(32), .enable("false")) multiplexer_2 (
    .in0(INSTRUCTION), .in1(32'h13), .out(multiplexer_2_out), .sel(pcsel));
  Adder #(.width(32)) adder_2 (.a(pc_value), .b(32'h4), .out(pc_value_plus_4));  // open: cin, cout
  Register #(.width(32)) register_1 (.D(PROGRAM_COUNTER), .clk(CLOCK), .Q(pc_value));  // open: en, clr
  Register #(.width(32)) register_2 (.D(multiplexer_2_out), .clk(CLOCK), .Q(instruction_curr));  // open: en, clr
  imm_gen imm_gen_1 (.ImmSel(immsel), .imm(imm), .inst(instruction_curr));
  branch_comp branch_comp_1 (.BrEq(breq), .BrUn(brun), .rs1(rs1), .BrLt(brlt), .rs2(rs2));
  regfile_main RegFile (
    .rs2(instruction_curr[24:20]), .rd(instruction_curr[11:7]), .Read_Data_1(rs1), .Read_Data_2(rs2),
    .ra(ra), .sp(sp), .t0(t0), .t1(t1), .t2(t2), .s0(s0), .s1(s1), .a0(a0), .rs1(instruction_curr[19:15]),
    .Write_Data(wb), .RegWEn(regwen), .clk(CLOCK));
  Multiplexer #(.width(32), .enable("false")) multiplexer_3 (
    .in0(rs1), .in1(pc_value), .out(multiplexer_3_out), .sel(asel));
  Multiplexer #(.width(32), .enable("false")) multiplexer_4 (.in0(rs2), .in1(imm), .out(multiplexer_4_out), .sel(bsel));
  // mem_main DMEM: pin names not known; wires that end beside it: alu_result, rs2, CLOCK, memrw, output_dmem, memrw, alu_result
  alu Arithmetic_Logic_Unit (.ALUSel(alusel), .Result(alu_result), .A(multiplexer_3_out), .B(multiplexer_4_out));
  Multiplexer #(.select(2), .width(32), .enable("false")) multiplexer_5 (
    .in0(pc_value_plus_4), .in1(alu_result), .in2(dmem), .in3(imm), .out(wb), .sel(wbsel));
  aftedmem aftedmem_1 (
    .addr(alu_result), .funct3(instruction_curr[14:12]), .output_dmem(output_dmem), .real_output(dmem));

  // Other names for the same wires on the sheet: clk = CLOCK

  // Notes on the sheet:
  //   Output
  //   IMEM (do **NOT** move this)
  //   Inputs
  //   It is OK to move the PC, RegFile, ALU, MEM, Branch Comp, Imm Gen, and Control Logic to wherever is most convenient for you when constructing your CPU, and to delete this text
  //   Inputs/Outputs for testing. Do **NOT** move these.
endmodule

module aftedmem (
  input  [31:0] addr,
  input  [2:0] funct3,
  input  [31:0] output_dmem,
  output [31:0] real_output
);

  wire [31:0] byte0, byte1, byte2, byte3, half0, half1, lb, lh;

  assign byte0 = {{24{output_dmem[7]}}, output_dmem[7:0]};  // Bit_Extender bit_extender_1
  assign byte1 = {{24{output_dmem[15]}}, output_dmem[15:8]};  // Bit_Extender bit_extender_2
  assign byte2 = {{24{output_dmem[23]}}, output_dmem[23:16]};  // Bit_Extender bit_extender_3
  assign byte3 = {{24{output_dmem[31]}}, output_dmem[31:24]};  // Bit_Extender bit_extender_4
  assign half0 = {{16{output_dmem[15]}}, output_dmem[15:0]};  // Bit_Extender bit_extender_5
  assign half1 = {{16{output_dmem[31]}}, output_dmem[31:16]};  // Bit_Extender bit_extender_6
  Multiplexer #(.select(2), .width(32), .enable("false")) multiplexer_1 (
    .in0(byte0), .in1(byte1), .in2(byte2), .in3(byte3), .out(lb), .sel(addr[1:0]));
  Multiplexer #(.width(32), .enable("false")) multiplexer_2 (.in0(half0), .in1(half1), .out(lh), .sel(addr[1]));
  Multiplexer #(.select(2), .width(32), .enable("false")) multiplexer_3 (
    .in0(lb), .in1(lh), .in2(output_dmem), .out(real_output), .sel(funct3[1:0]));  // open: in3

  // Other names for the same wires on the sheet: lw[31:0] = output_dmem
endmodule
